# Fritzing sketch PH-EC-Temp (saved by Fritzing 0.9.3b)
breadboards: 1

parts:
  part = Arduino Nano (Rev3.0)
  S1 = Pushbutton [package="[THT]"]
  S2 = Pushbutton [package="[THT]"]
  R1 = Resistor [tolerance=±5% resistance=68k package=THT]
  R2 = Resistor [tolerance=±5% resistance=15k package=THT]
  R3 = Resistor [tolerance=±5% resistance=220 package=THT]
  D1 = Rectifier Diode [part_number=1N4001 package="300 mil [THT]"]
  C1 = Electrolytic Capacitor [capacitance=0.22mF voltage=20V package="100 mil [THT, electrolytic]"]
  FAN_12V = DC Motor
  TIP120 = npn-Powertransistor [package="TO220 [THT]"]
  100k_NTC = Temperature Sensor (Thermistor) [thermistor_type=NTC package=THT]
  10k_NTC = Temperature Sensor (Thermistor) [thermistor_type=NTC package=THT]
  R4 = Resistor [tolerance=±5% resistance=2.2k package=THT]
  R5 = Resistor [tolerance=±5% resistance=2.2k package=THT]
  EC = female pin header, 2 pins [form="♀ (female)"]
  SCL_SDA_for_lcd_4x20 = female pin header, 2 pins [form="♀ (female)"]
  PH = mystery part, 3 pins [chip_label=PH-modul]

nets:
  N1: part.GND, S1.Pin_3, S1.Pin_4, S2.Pin_3, S2.Pin_4, TIP120.emitter, 100k_NTC.pin_0, 10k_NTC.pin_0, PH.pin2
  N2: part.D4, R5.Pin_0
  N3: part.D5, R4.Pin_0
  N4: part.D6, R3.Pin_0
  N5: part.D11/MOSI, S2.Pin_1, S2.Pin_2
  N6: part.D12/MISO, S1.Pin_1, S1.Pin_2
  N7: part.5V, R1.Pin_1, R2.Pin_1, PH.pin1
  N8: part.A7, R5.Pin_1, EC.pin2
  N9: part.A6, R4.Pin_1, EC.pin1
  N10: part.A5, SCL_SDA_for_lcd_4x20.pin2
  N11: part.A4, SCL_SDA_for_lcd_4x20.pin1
  N12: part.A2, R2.Pin_0, 10k_NTC.pin_1
  N13: part.A1, PH.pin3
  N14: part.A0, R1.Pin_0, 100k_NTC.pin_1
  N15: R3.Pin_1, TIP120.base
  12V: D1.cathode, C1.+, FAN_12V.pin_1
  N16: D1.anode, C1.-, FAN_12V.pin_2, TIP120.collector
